# Fritzing sketch Carga_Activa_(2) (saved by Fritzing 0.9.3b)
perfboards: 1

parts:
  U1 = ESP32S-HiLetgo [part_number=ESP32S]  # not connected
  R14 = Resistor [tolerance=±5% resistance=220 package=THT]  # not connected
  Q1 = Basic FET N-Channel [package="TO220 [THT]"]
  C2 = Electrolytic Capacitor top view [package="100 mil [THT, electrolytic]"]
  R13 = Resistor [tolerance=±5% resistance=220 package=THT]  # not connected
  C8 = Electrolytic Capacitor top view [package="100 mil [THT, electrolytic]"]  # not connected
  D2 = Upright Rectifier Diode [part_number=1N4006 package="300 mil [THT]"]
  D1 = Upright Rectifier Diode [part_number=1N4006 package="300 mil [THT]"]  # not connected
  C7 = Electrolytic Capacitor top view [package="100 mil [THT, electrolytic]"]  # not connected
  R5 = Resistor [tolerance=±5% resistance=0 package=THT]
  C9 = Ceramic Capacitor top view [package="100 mil [THT, multilayer]"]
  IC2 = H-Bridge [package=THT]
  IC3 = IC, DIP package, 8 pins [chip_label=IC]
  R1 = Resistor [tolerance=±5% resistance=220 package=THT]  # not connected
  C2_2 = Ceramic Capacitor top view [package="100 mil [THT, multilayer]"]
  C1 = Ceramic Capacitor top view [package="100 mil [THT, multilayer]"]  # not connected
  R3 = Resistor [tolerance=±5% resistance=220 package=THT]  # not connected
  R4 = Resistor [tolerance=±5% resistance=220 package=THT]
  R7 = Resistor [tolerance=±5% resistance=220 package=THT]
  R6 = Resistor [tolerance=±5% resistance=220 package=THT]
  C3 = Ceramic Capacitor top view [package="100 mil [THT, multilayer]"]
  R8 = Vertical Resistor [tolerance=±5% resistance=220 package=THT]
  R9 = Vertical Resistor [tolerance=±5% resistance=220 package=THT]
  C4 = Ceramic Capacitor top view [package="100 mil [THT, multilayer]"]  # not connected
  R10 = Resistor [tolerance=±5% resistance=220 package=THT]  # not connected
  J1 = Camdenboss CTB0158-3 [part_number=CTB0158-3 package=THT]  # not connected
  R12 = Vertical Resistor [tolerance=±5% resistance=220 package=THT]  # not connected
  C11 = Ceramic Capacitor top view [package="100 mil [THT, multilayer]"]  # not connected
  R11 = Resistor [tolerance=±5% resistance=220 package=THT]  # not connected
  C5 = Electrolytic Capacitor top view [package="100 mil [THT, electrolytic]"]
  R15 = Vertical Resistor [tolerance=±5% resistance=220 package=THT]  # not connected

nets:
  N1: Q1.gate, R4.Pin_1
  N2: Q1.drain, R7.Pin_0
  N3: C2.+, C9.1, C3.0, C5.+
  N4: D2.cathode, C2_2.1
  N5: R5.Pin_1, IC2.VCC2, R6.Pin_1
  N6: IC3.pin1, IC3.pin6
  N7: IC3.pin8, C3.1, R9.Pin_0, C5.-
  N8: R7.Pin_1, R6.Pin_0
  N9: R8.Pin_0, R9.Pin_1

custom parts:
  ESP32S-HiLetgo: HiLetgo ESP-WROOM-32 ESP32 ESP-32S Development Board 2.4GHz Dual-Mode WiFi + Bluetooth Dual Cores Microcontroller The ESP32 integrated with Antenna switches, RF Balun, power amplifiers, low-noise amplifiers, filters, and management modules, and the entire solution occupies the least area of PCB. 2.4 GHz Wi-Fi plus Bluetooth dual-mode chip, with TSMC Ultra-low power consumption 40nm technology,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
  Electrolytic Capacitor top view: A small electrolytic capacitor breadboard top view for use on perf board
  Upright Rectifier Diode: A standard rectifier diode Based on Brendan Howell's work
  Ceramic Capacitor top view: 100 nF multilayer Ceramic Capacitor breadboard set to top view for perfboard use.
  Vertical Resistor: A generic resistor (0.25W)
