# Fritzing sketch Esquema_Carga_Activa-Aitor-2 (saved by Fritzing 0.9.3b)
perfboards: 1

parts:
  ESP32 = ESP32S-HiLetgo [part_number=ESP32S]  # not connected
  R14 = Resistor [tolerance=±5% resistance=220 package=THT]
  Q1 = Basic FET N-Channel [package="TO220 [THT]"]
  C2 = Electrolytic Capacitor top view [package="100 mil [THT, electrolytic]"]
  R13 = Resistor [tolerance=±5% resistance=220 package=THT]
  C8 = Electrolytic Capacitor top view [package="100 mil [THT, electrolytic]"]
  D2 = Upright Rectifier Diode [part_number=1N4006 package="300 mil [THT]"]
  D1 = Upright Rectifier Diode [part_number=1N4006 package="300 mil [THT]"]
  C7 = Electrolytic Capacitor top view [package="100 mil [THT, electrolytic]"]
  R5 = Resistor [tolerance=±5% resistance=0 package=THT]
  C9 = Ceramic Capacitor top view [package="100 mil [THT, multilayer]"]
  IC2 = H-Bridge [package=THT]
  IC3 = IC, DIP package, 8 pins [chip_label=IC]
  R1 = Resistor [tolerance=±5% resistance=220 package=THT]  # not connected
  C2_2 = Ceramic Capacitor top view [package="100 mil [THT, multilayer]"]
  C1 = Ceramic Capacitor top view [package="100 mil [THT, multilayer]"]  # not connected
  R3 = Resistor [tolerance=±5% resistance=220 package=THT]  # not connected
  R4 = Resistor [tolerance=±5% resistance=220 package=THT]
  R7 = Resistor [tolerance=±5% resistance=220 package=THT]
  R6 = Resistor [tolerance=±5% resistance=220 package=THT]
  R8 = Vertical Resistor [tolerance=±5% resistance=220 package=THT]
  R9 = Vertical Resistor [tolerance=±5% resistance=220 package=THT]
  C4 = Ceramic Capacitor top view [package="100 mil [THT, multilayer]"]
  R10 = Resistor [tolerance=±5% resistance=220 package=THT]  # not connected
  J1 = Camdenboss CTB0158-3 [part_number=CTB0158-3 package=THT]  # not connected
  R12 = Vertical Resistor [tolerance=±5% resistance=220 package=THT]
  R11 = Resistor [tolerance=±5% resistance=220 package=THT]
  C5 = Electrolytic Capacitor top view [package="100 mil [THT, electrolytic]"]
  R15 = Vertical Resistor [tolerance=±5% resistance=220 package=THT]
  R16 = Vertical Resistor [tolerance=±5% resistance=220 package=THT]  # not connected
  C12 = Ceramic Capacitor top view [package="100 mil [THT, multilayer]"]  # not connected
  Q2 = NPN-Transistor [package="TO92 [THT]"]
  R15_2 = Resistor [tolerance=±5% resistance=220 package=THT]
  D3 = Upright Rectifier Diode [part_number=1N4006 package="300 mil [THT]"]
  C13 = Ceramic Capacitor top view [package="100 mil [THT, multilayer]"]

nets:
  N1: R14.Pin_1, C8.+
  N2: Q1.gate, R4.Pin_1
  N3: Q1.drain, R7.Pin_0
  N4: C2.-, D2.anode, C7.+, R5.Pin_1, C2_2.0, R6.Pin_1, R15.Pin_1
  N5: C2.+, C9.0, IC2.4A, R12.Pin_1, R11.Pin_1, C5.-, C5.+, C13.0
  N6: R13.Pin_1, D1.cathode, C7.-
  N7: C8.-, D2.cathode, D1.anode
  N8: IC2.1A, D3.cathode
  N9: IC3.pin1, IC3.pin6
  N10: IC3.pin7, R15.Pin_0
  N11: R7.Pin_1, R6.Pin_0
  N12: R8.Pin_0, R9.Pin_1
  N13: R9.Pin_0, C4.0
  N14: Q2.B, R15_2.Pin_0

custom parts:
  ESP32S-HiLetgo: HiLetgo ESP-WROOM-32 ESP32 ESP-32S Development Board 2.4GHz Dual-Mode WiFi + Bluetooth Dual Cores Microcontroller The ESP32 integrated with Antenna switches, RF Balun, power amplifiers, low-noise amplifiers, filters, and management modules, and the entire solution occupies the least area of PCB. 2.4 GHz Wi-Fi plus Bluetooth dual-mode chip, with TSMC Ultra-low power consumption 40nm technology,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
  Electrolytic Capacitor top view: A small electrolytic capacitor breadboard top view for use on perf board
  Upright Rectifier Diode: A standard rectifier diode Based on Brendan Howell's work
  Ceramic Capacitor top view: 100 nF multilayer Ceramic Capacitor breadboard set to top view for perfboard use.
  Vertical Resistor: A generic resistor (0.25W)
